// Logisim project display_ship.circ as structural Verilog: 1 circuit, main circuit display_ship
module display_ship (
  input  [1:0] num_picture,
  output [19:0] out_2,
  output [19:0] out_3,
  output [19:0] out_4,
  output [19:0] out_5,
  output [19:0] out_6,
  output [19:0] out_7,
  output [19:0] out_8,
  output [19:0] out_9,
  output [19:0] out_10,
  output [19:0] out_11,
  output [19:0] out_12,
  output [19:0] out_13,
  output [19:0] out_14,
  output [19:0] out_15,
  output [19:0] out_16,
  output [19:0] out_17,
  output [19:0] out_18,
  output [19:0] out_19,
  output [19:0] out_20,
  output [19:0] out_21,
  output [19:0] out_22,
  output [19:0] out_23,
  output [19:0] out_24,
  output [19:0] out_25,
  output [19:0] out_26,
  output [19:0] out_27,
  output [19:0] out_28,
  output [19:0] out_29,
  output [19:0] out_30,
  output [19:0] out_31,
  output [19:0] out_32,
  output [19:0] out_33
);

  wire is_1, is_2, is_3, is_4;
  wire [3:1] _1_5, _1_7, _1_8, _1_10, _1_11, _1_14, _1_16, _1_17, _1_19, _1_20, _1_22, _1_23;
  wire [3:3] _1_4, _1_29;
  wire [4:2] _3_27, _3_28, _3_29, _3_30, _3_31, _4_2, _4_3, _4_4, _4_5, _4_6;
  wire [5:1] _1_6, _1_9, _1_12, _1_15, _1_18, _1_21;
  wire [5:3] _1_3, _1_30;
  wire [9:1] _1_13;
  wire [9:9] _1_2;
  wire [13:1] _1_24, _1_25, _1_26, _1_27, _1_28;
  wire [17:17] _2_9;
  wire [18:18] _2_10;
  wire [19:0] _2_5, _2_28;
  wire [19:1] _2_4, _2_29;
  wire [19:2] _2_3, _2_30;
  wire [19:3] _2_2, _2_31;
  wire [19:4] _2_1, _2_32;
  wire [19:8] _2_18, _2_19, _2_20;
  wire [19:15] _2_7;
  wire [19:16] _2_8;
  wire [19:19] _2_6, _2_11, _2_12, _2_13, _2_14, _2_15, _2_16, _2_17, _2_21, _2_22, _2_23, _2_24, _2_25,
       _2_26, _2_27;

  assign out_2 = is_1 ? 20'h60 : 20'bz;  // Controlled_Buffer controlled_buffer_1
  assign out_2 = is_2 ? {{13{_2_1[19]}}, 2'b11, {5{_2_1[4]}}} : 20'bz;  // Controlled_Buffer controlled_buffer_2
  assign out_2 = is_3 ? {20{1'b0}} : 20'bz;  // Controlled_Buffer controlled_buffer_3
  assign out_2 = is_4 ? 20'h200 : 20'bz;  // Controlled_Buffer controlled_buffer_4
  assign out_3 = is_1 ? {{10{1'b0}}, _1_2[9], 9'h70} : 20'bz;  // Controlled_Buffer controlled_buffer_5
  assign out_3 = is_2 ? {{13{_2_2[19]}}, 3'b111, {4{_2_2[3]}}} : 20'bz;  // Controlled_Buffer controlled_buffer_6
  assign out_3 = is_3 ? 20'h7e790 : 20'bz;  // Controlled_Buffer controlled_buffer_7
  assign out_3 = is_4 ? {15'h1019, _4_2[4], 1'b1, _4_2[2], 2'b11} : 20'bz;  // Controlled_Buffer controlled_buffer_8
  assign out_4 = is_1 ? {14'h9, _1_3[5], 1'b1, _1_3[3], 3'b000} : 20'bz;  // Controlled_Buffer controlled_buffer_9
  assign out_4 = is_2 ? {{13{_2_3[19]}}, 4'b1010, {3{_2_3[2]}}} : 20'bz;  // Controlled_Buffer controlled_buffer_10
  assign out_4 = is_3 ? 20'h52490 : 20'bz;  // Controlled_Buffer controlled_buffer_11
  assign out_4 = is_4 ? {15'h100d, _4_3[4], 1'b1, _4_3[2], 2'b11} : 20'bz;  // Controlled_Buffer controlled_buffer_12
  assign out_5 = is_1 ? {16'h2f, _1_4[3], 3'b100} : 20'bz;  // Controlled_Buffer controlled_buffer_13
  assign out_5 = is_2 ? {{13{_2_4[19]}}, 5'b11101, {2{_2_4[1]}}} : 20'bz;  // Controlled_Buffer controlled_buffer_14
  assign out_5 = is_3 ? 20'h52490 : 20'bz;  // Controlled_Buffer controlled_buffer_15
  assign out_5 = is_4 ? {15'h1fc5, _4_4[4], 1'b1, _4_4[2], 2'b11} : 20'bz;  // Controlled_Buffer controlled_buffer_16
  assign out_6 = is_1 ? {16'h3f, _1_5[3], 1'b1, _1_5[1], 1'b0} : 20'bz;  // Controlled_Buffer controlled_buffer_17
  assign out_6 = is_2 ? {{5{_2_5[19]}}, 14'h2bfa, _2_5[0]} : 20'bz;  // Controlled_Buffer controlled_buffer_18
  assign out_6 = is_3 ? 20'h2c4f0 : 20'bz;  // Controlled_Buffer controlled_buffer_19
  assign out_6 = is_4 ? {15'h1001, _4_5[4], 1'b1, _4_5[2], 2'b11} : 20'bz;  // Controlled_Buffer controlled_buffer_20
  assign out_7 = is_1 ? {14'h1f, _1_6[5], 1'b1, _1_6[3], 1'b1, _1_6[1], 1'b1} : 20'bz;  // Controlled_Buffer controlled_buffer_21
  assign out_7 = is_2 ? {{5{_2_6[19]}}, 15'h57d5} : 20'bz;  // Controlled_Buffer controlled_buffer_22
  assign out_7 = is_3 ? {20{1'b0}} : 20'bz;  // Controlled_Buffer controlled_buffer_23
  assign out_7 = is_4 ? {15'h1001, _4_6[4], 1'b1, _4_6[2], 2'b11} : 20'bz;  // Controlled_Buffer controlled_buffer_24
  assign out_8 = is_1 ? {16'h7f, _1_7[3], 1'b1, _1_7[1], 1'b1} : 20'bz;  // Controlled_Buffer controlled_buffer_25
  assign out_8 = is_2 ? {{2{_2_7[19]}}, 2'b11, _2_7[15], 15'h57f5} : 20'bz;  // Controlled_Buffer controlled_buffer_26
  assign out_8 = is_3 ? {20{1'b0}} : 20'bz;  // Controlled_Buffer controlled_buffer_27
  assign out_8 = is_4 ? {20{1'b0}} : 20'bz;  // Controlled_Buffer controlled_buffer_28
  assign out_9 = is_1 ? {16'h3f, _1_8[3], 1'b1, _1_8[1], 1'b1} : 20'bz;  // Controlled_Buffer controlled_buffer_29
  assign out_9 = is_2 ? {_2_8[19], 2'b11, {2{_2_8[16]}}, 15'h57f5} : 20'bz;  // Controlled_Buffer controlled_buffer_30
  assign out_9 = is_3 ? 20'h1e7f0 : 20'bz;  // Controlled_Buffer controlled_buffer_31
  assign out_9 = is_4 ? 20'h3f800 : 20'bz;  // Controlled_Buffer controlled_buffer_32
  assign out_10 = is_1 ? {14'h3, _1_9[5], 1'b1, _1_9[3], 1'b1, _1_9[1], 1'b1} : 20'bz;  // Controlled_Buffer controlled_buffer_33
  assign out_10 = is_2 ? {2'b11, {3{_2_9[17]}}, 15'h57d5} : 20'bz;  // Controlled_Buffer controlled_buffer_34
  assign out_10 = is_3 ? 20'h28080 : 20'bz;  // Controlled_Buffer controlled_buffer_35
  assign out_10 = is_4 ? 20'h4000 : 20'bz;  // Controlled_Buffer controlled_buffer_36
  assign out_11 = is_1 ? {16'h7, _1_10[3], 1'b1, _1_10[1], 1'b1} : 20'bz;  // Controlled_Buffer controlled_buffer_37
  assign out_11 = is_2 ? {1'b1, {12{_2_10[18]}}, 7'b1110101} : 20'bz;  // Controlled_Buffer controlled_buffer_38
  assign out_11 = is_3 ? 20'h3e080 : 20'bz;  // Controlled_Buffer controlled_buffer_39
  assign out_11 = is_4 ? 20'h4000 : 20'bz;  // Controlled_Buffer controlled_buffer_40
  assign out_12 = is_1 ? {16'h7, _1_11[3], 1'b1, _1_11[1], 1'b1} : 20'bz;  // Controlled_Buffer controlled_buffer_41
  assign out_12 = is_2 ? {{13{_2_11[19]}}, 7'b1110101} : 20'bz;  // Controlled_Buffer controlled_buffer_42
  assign out_12 = is_3 ? 20'h7f0 : 20'bz;  // Controlled_Buffer controlled_buffer_43
  assign out_12 = is_4 ? 20'h4000 : 20'bz;  // Controlled_Buffer controlled_buffer_44
  assign out_13 = is_1 ? {14'h1, _1_12[5], 1'b1, _1_12[3], 1'b1, _1_12[1], 1'b1} : 20'bz;  // Controlled_Buffer controlled_buffer_45
  assign out_13 = is_2 ? {{13{_2_12[19]}}, 7'b1010101} : 20'bz;  // Controlled_Buffer controlled_buffer_46
  assign out_13 = is_3 ? 20'h20000 : 20'bz;  // Controlled_Buffer controlled_buffer_47
  assign out_13 = is_4 ? 20'h3f800 : 20'bz;  // Controlled_Buffer controlled_buffer_48
  assign out_14 = is_1 ? {{10{1'b0}}, _1_13[9], 5'b00111, _1_13[3], 1'b1, _1_13[1], 1'b1} : 20'bz;  // Controlled_Buffer controlled_buffer_49
  assign out_14 = is_2 ? {{12{_2_13[19]}}, 8'hf5} : 20'bz;  // Controlled_Buffer controlled_buffer_50
  assign out_14 = is_3 ? 20'h3e000 : 20'bz;  // Controlled_Buffer controlled_buffer_51
  assign out_14 = is_4 ? {20{1'b0}} : 20'bz;  // Controlled_Buffer controlled_buffer_52
  assign out_15 = is_1 ? {16'h27, _1_14[3], 1'b1, _1_14[1], 1'b1} : 20'bz;  // Controlled_Buffer controlled_buffer_53
  assign out_15 = is_2 ? {{10{_2_14[19]}}, 10'h3f5} : 20'bz;  // Controlled_Buffer controlled_buffer_54
  assign out_15 = is_3 ? 20'h20410 : 20'bz;  // Controlled_Buffer controlled_buffer_55
  assign out_15 = is_4 ? 20'h3fbf8 : 20'bz;  // Controlled_Buffer controlled_buffer_56
  assign out_16 = is_1 ? {14'hb, _1_15[5], 1'b1, _1_15[3], 1'b1, _1_15[1], 1'b1} : 20'bz;  // Controlled_Buffer controlled_buffer_57
  assign out_16 = is_2 ? {{9{_2_15[19]}}, 11'h7d5} : 20'bz;  // Controlled_Buffer controlled_buffer_58
  assign out_16 = is_3 ? 20'h410 : 20'bz;  // Controlled_Buffer controlled_buffer_59
  assign out_16 = is_4 ? 20'h24a48 : 20'bz;  // Controlled_Buffer controlled_buffer_60
  assign out_17 = is_1 ? {16'h3f, _1_16[3], 1'b1, _1_16[1], 1'b1} : 20'bz;  // Controlled_Buffer controlled_buffer_61
  assign out_17 = is_2 ? {{9{_2_16[19]}}, 11'h7f5} : 20'bz;  // Controlled_Buffer controlled_buffer_62
  assign out_17 = is_3 ? 20'h207f0 : 20'bz;  // Controlled_Buffer controlled_buffer_63
  assign out_17 = is_4 ? 20'h24a48 : 20'bz;  // Controlled_Buffer controlled_buffer_64
  assign out_18 = is_1 ? {16'h7f, _1_17[3], 1'b1, _1_17[1], 1'b1} : 20'bz;  // Controlled_Buffer controlled_buffer_65
  assign out_18 = is_2 ? {{10{_2_17[19]}}, 10'h3f5} : 20'bz;  // Controlled_Buffer controlled_buffer_66
  assign out_18 = is_3 ? 20'h3e410 : 20'bz;  // Controlled_Buffer controlled_buffer_67
  assign out_18 = is_4 ? 20'h24a48 : 20'bz;  // Controlled_Buffer controlled_buffer_68
  assign out_19 = is_1 ? {14'h1f, _1_18[5], 1'b1, _1_18[3], 1'b1, _1_18[1], 1'b1} : 20'bz;  // Controlled_Buffer controlled_buffer_69
  assign out_19 = is_2 ? {{10{_2_18[19]}}, 1'b1, _2_18[8], 8'hd5} : 20'bz;  // Controlled_Buffer controlled_buffer_70
  assign out_19 = is_3 ? 20'h20410 : 20'bz;  // Controlled_Buffer controlled_buffer_71
  assign out_19 = is_4 ? 20'h24a48 : 20'bz;  // Controlled_Buffer controlled_buffer_72
  assign out_20 = is_1 ? {16'h3f, _1_19[3], 1'b1, _1_19[1], 1'b1} : 20'bz;  // Controlled_Buffer controlled_buffer_73
  assign out_20 = is_2 ? {{10{_2_19[19]}}, 1'b1, {2{_2_19[8]}}, 7'b1110101} : 20'bz;  // Controlled_Buffer controlled_buffer_74
  assign out_20 = is_3 ? {20{1'b0}} : 20'bz;  // Controlled_Buffer controlled_buffer_75
  assign out_20 = is_4 ? {20{1'b0}} : 20'bz;  // Controlled_Buffer controlled_buffer_76
  assign out_21 = is_1 ? {16'hf, _1_20[3], 1'b1, _1_20[1], 1'b1} : 20'bz;  // Controlled_Buffer controlled_buffer_77
  assign out_21 = is_2 ? {{10{_2_20[19]}}, 1'b0, {2{_2_20[8]}}, 7'b1110101} : 20'bz;  // Controlled_Buffer controlled_buffer_78
  assign out_21 = is_3 ? 20'h3e000 : 20'bz;  // Controlled_Buffer controlled_buffer_79
  assign out_21 = is_4 ? 20'h3f8 : 20'bz;  // Controlled_Buffer controlled_buffer_80
  assign out_22 = is_1 ? {14'h1, _1_21[5], 1'b1, _1_21[3], 1'b1, _1_21[1], 1'b1} : 20'bz;  // Controlled_Buffer controlled_buffer_81
  assign out_22 = is_2 ? {{13{_2_21[19]}}, 7'b1010101} : 20'bz;  // Controlled_Buffer controlled_buffer_82
  assign out_22 = is_3 ? 20'h27f0 : 20'bz;  // Controlled_Buffer controlled_buffer_83
  assign out_22 = is_4 ? 20'h80 : 20'bz;  // Controlled_Buffer controlled_buffer_84
  assign out_23 = is_1 ? {16'h7, _1_22[3], 1'b1, _1_22[1], 1'b1} : 20'bz;  // Controlled_Buffer controlled_buffer_85
  assign out_23 = is_2 ? {{13{_2_22[19]}}, 7'b1110101} : 20'bz;  // Controlled_Buffer controlled_buffer_86
  assign out_23 = is_3 ? 20'h480 : 20'bz;  // Controlled_Buffer controlled_buffer_87
  assign out_23 = is_4 ? 20'h40 : 20'bz;  // Controlled_Buffer controlled_buffer_88
  assign out_24 = is_1 ? {16'h8007, _1_23[3], 1'b1, _1_23[1], 1'b1} : 20'bz;  // Controlled_Buffer controlled_buffer_89
  assign out_24 = is_2 ? {{13{_2_23[19]}}, 7'b1110101} : 20'bz;  // Controlled_Buffer controlled_buffer_90
  assign out_24 = is_3 ? 20'h3e480 : 20'bz;  // Controlled_Buffer controlled_buffer_91
  assign out_24 = is_4 ? 20'h20 : 20'bz;  // Controlled_Buffer controlled_buffer_92
  assign out_25 = is_1 ? {6'b110001, _1_24[13], 1'b1, _1_24[11], {5{1'b1}}, _1_24[5], 1'b1, _1_24[3], 1'b1, _1_24[1], 1'b1} : 20'bz;  // Controlled_Buffer controlled_buffer_93
  assign out_25 = is_2 ? {{12{_2_24[19]}}, 8'hd5} : 20'bz;  // Controlled_Buffer controlled_buffer_94
  assign out_25 = is_3 ? 20'h2a780 : 20'bz;  // Controlled_Buffer controlled_buffer_95
  assign out_25 = is_4 ? 20'h3f8 : 20'bz;  // Controlled_Buffer controlled_buffer_96
  assign out_26 = is_1 ? {6'b011001, _1_25[13], 1'b1, _1_25[11], {7{1'b1}}, _1_25[3], 1'b1, _1_25[1], 1'b1} : 20'bz;  // Controlled_Buffer controlled_buffer_97
  assign out_26 = is_2 ? {{10{_2_25[19]}}, 10'h3f5} : 20'bz;  // Controlled_Buffer controlled_buffer_98
  assign out_26 = is_3 ? {20{1'b0}} : 20'bz;  // Controlled_Buffer controlled_buffer_99
  assign out_26 = is_4 ? {20{1'b0}} : 20'bz;  // Controlled_Buffer controlled_buffer_100
  assign out_27 = is_1 ? {6'b001101, _1_26[13], 1'b1, _1_26[11], {7{1'b1}}, _1_26[3], 1'b1, _1_26[1], 1'b1} : 20'bz;  // Controlled_Buffer controlled_buffer_101
  assign out_27 = is_2 ? {{9{_2_26[19]}}, 11'h7f5} : 20'bz;  // Controlled_Buffer controlled_buffer_102
  assign out_27 = is_3 ? {20{1'b0}} : 20'bz;  // Controlled_Buffer controlled_buffer_103
  assign out_27 = is_4 ? 20'h3f8 : 20'bz;  // Controlled_Buffer controlled_buffer_104
  assign out_28 = is_1 ? {6'b000001, _1_27[13], 1'b1, _1_27[11], {5{1'b1}}, _1_27[5], 1'b1, _1_27[3], 1'b1, _1_27[1], 1'b1} : 20'bz;  // Controlled_Buffer controlled_buffer_105
  assign out_28 = is_2 ? {{9{_2_27[19]}}, 11'h7d5} : 20'bz;  // Controlled_Buffer controlled_buffer_106
  assign out_28 = is_3 ? {15'h1, _3_27[4], 1'b1, _3_27[2], 2'b11} : 20'bz;  // Controlled_Buffer controlled_buffer_107
  assign out_28 = is_4 ? 20'h208 : 20'bz;  // Controlled_Buffer controlled_buffer_108
  assign out_29 = is_1 ? {6'b000001, _1_28[13], 1'b1, _1_28[11], {7{1'b1}}, _1_28[3], 1'b1, _1_28[1], 1'b0} : 20'bz;  // Controlled_Buffer controlled_buffer_109
  assign out_29 = is_2 ? {{10{_2_28[19]}}, 9'h1fa, _2_28[0]} : 20'bz;  // Controlled_Buffer controlled_buffer_110
  assign out_29 = is_3 ? {15'h1, _3_28[4], 1'b1, _3_28[2], 2'b11} : 20'bz;  // Controlled_Buffer controlled_buffer_111
  assign out_29 = is_4 ? 20'h208 : 20'bz;  // Controlled_Buffer controlled_buffer_112
  assign out_30 = is_1 ? {16'h7, _1_29[3], 3'b100} : 20'bz;  // Controlled_Buffer controlled_buffer_113
  assign out_30 = is_2 ? {{10{_2_29[19]}}, 1'b1, _2_29[8], 6'b111101, {2{_2_29[1]}}} : 20'bz;  // Controlled_Buffer controlled_buffer_114
  assign out_30 = is_3 ? {15'h5, _3_29[4], 1'b1, _3_29[2], 2'b11} : 20'bz;  // Controlled_Buffer controlled_buffer_115
  assign out_30 = is_4 ? 20'h208 : 20'bz;  // Controlled_Buffer controlled_buffer_116
  assign out_31 = is_1 ? {14'h1, _1_30[5], 1'b1, _1_30[3], 3'b000} : 20'bz;  // Controlled_Buffer controlled_buffer_117
  assign out_31 = is_2 ? {{10{_2_30[19]}}, 1'b1, {2{_2_30[8]}}, 4'b1010, {3{_2_30[2]}}} : 20'bz;  // Controlled_Buffer controlled_buffer_118
  assign out_31 = is_3 ? {15'hd, _3_30[4], 1'b1, _3_30[2], 2'b11} : 20'bz;  // Controlled_Buffer controlled_buffer_119
  assign out_31 = is_4 ? 20'h1f0 : 20'bz;  // Controlled_Buffer controlled_buffer_120
  assign out_32 = is_1 ? 20'h70 : 20'bz;  // Controlled_Buffer controlled_buffer_121
  assign out_32 = is_2 ? {{10{_2_31[19]}}, 1'b0, {2{_2_31[8]}}, 3'b111, {4{_2_31[3]}}} : 20'bz;  // Controlled_Buffer controlled_buffer_122
  assign out_32 = is_3 ? {15'h19, _3_31[4], 1'b1, _3_31[2], 2'b11} : 20'bz;  // Controlled_Buffer controlled_buffer_123
  assign out_32 = is_4 ? {20{1'b0}} : 20'bz;  // Controlled_Buffer controlled_buffer_124
  assign out_33 = is_1 ? 20'h60 : 20'bz;  // Controlled_Buffer controlled_buffer_125
  assign out_33 = is_2 ? {{13{_2_32[19]}}, 2'b11, {5{_2_32[4]}}} : 20'bz;  // Controlled_Buffer controlled_buffer_126
  assign out_33 = is_3 ? 20'h600 : 20'bz;  // Controlled_Buffer controlled_buffer_127
  assign out_33 = is_4 ? {20{1'b0}} : 20'bz;  // Controlled_Buffer controlled_buffer_128
  Demultiplexer #(.select(2), .enable("false")) demultiplexer_1 (
    .out0(is_1), .out1(is_2), .out2(is_3), .out3(is_4), .in(1'b1), .sel(num_picture));

  // Other names for the same wires on the sheet: _2_1 (some bits) = {{12{_2_1[19]}}, {4{_2_1[4]}}};
  //   _2_2 (some bits) = {{12{_2_2[19]}}, {3{_2_2[3]}}}; _2_3 (some bits) = {{12{_2_3[19]}}, {2{_2_3[2]}}};
  //   _2_4 (some bits) = {{12{_2_4[19]}}, _2_4[1]}; _2_5[18:15] = {4{_2_5[19]}}; _2_6[18:15] = {4{_2_6[19]}};
  //   _2_7[18] = _2_7[19]; _2_8[15] = _2_8[16]; _2_9[16:15] = {2{_2_9[17]}}; _2_10[17:7] = {11{_2_10[18]}};
  //   _2_11[18:7] = {12{_2_11[19]}}; _2_12[18:7] = {12{_2_12[19]}}; _2_13[18:8] = {11{_2_13[19]}};
  //   _2_14[18:10] = {9{_2_14[19]}}; _2_15[18:11] = {8{_2_15[19]}}; _2_16[18:11] = {8{_2_16[19]}};
  //   _2_17[18:10] = {9{_2_17[19]}}; _2_18[18:10] = {9{_2_18[19]}}; _2_19 (some bits) = {{9{_2_19[19]}}, _2_19[8]};
  //   _2_20 (some bits) = {{9{_2_20[19]}}, _2_20[8]}; _2_21[18:7] = {12{_2_21[19]}}; _2_22[18:7] = {12{_2_22[19]}};
  //   _2_23[18:7] = {12{_2_23[19]}}; _2_24[18:8] = {11{_2_24[19]}}; _2_25[18:10] = {9{_2_25[19]}};
  //   _2_26[18:11] = {8{_2_26[19]}}; _2_27[18:11] = {8{_2_27[19]}}; _2_28[18:10] = {9{_2_28[19]}};
  //   _2_29 (some bits) = {{9{_2_29[19]}}, _2_29[1]}; _2_30 (some bits) = {{9{_2_30[19]}}, _2_30[8], {2{_2_30[2]}}};
  //   _2_31 (some bits) = {{9{_2_31[19]}}, _2_31[8], {3{_2_31[3]}}};
  //   _2_32 (some bits) = {{12{_2_32[19]}}, {4{_2_32[4]}}}
endmodule
